# Fritzing sketch board (saved by Fritzing 0.9.2b)
circuit board: 8.46667cm x 5.64444cm

parts:
  Arduino1 = Arduino Mini (Rev5)
  U1 = RF-LINK_TX [package=rf-link_tx]
  ANT1 = Antenna
  ENC28J2 = ENC28J60

nets (from the schematic view):
  GND: Arduino1.GND, U1.GND, ENC28J2.GND#12
  N1: Arduino1.D2, U1.DATA
  N2: Arduino1.D8, ENC28J2.CS
  VCC: Arduino1.VCC, ENC28J2.5v
  N3: Arduino1.D13, ENC28J2.SCK
  N4: Arduino1.D12, ENC28J2.INT, ENC28J2.SO
  N5: Arduino1.D11_PWM, ENC28J2.SI
  5V: Arduino1.5V, U1.+5V
  N6: U1.ANT, ANT1.antenna_lead

custom parts:
  ENC28J60: Ethernet Module ENC28J60
